# Fritzing sketch fritzing for lab1 (saved by Fritzing 0.9.2b)
breadboards: 1

parts:
  LED2 = LED - 5mm [color="Red (633nm)" package="5 mm [THT]"]
  R1 = Resistor [tolerance=±5% resistance=330 package=THT]
  R2 = Resistor [tolerance=±5% resistance=330 package=THT]
  R3 = Resistor [tolerance=±5% resistance=330 package=THT]
  Part1 = Arduino Uno (Rev3) - ICSP
  R4 = Resistor [tolerance=±5% resistance=220 package=THT]
  R5 = Resistor [tolerance=±5% resistance=220 package=THT]
  R6 = Photocell (LDR) [package=THT]
  R7 = Resistor [tolerance=±5% resistance=330 package=THT]
  R8 = Resistor [tolerance=±5% resistance=220 package=THT]
  SW1 = DIP Switch 8 Position [package=dipswitch-08]
  LED3 = RGB LED (com. cathode, rgb) [package="5 mm [THT]"]

nets:
  N1: LED2.cathode, R7.Pin_1
  N2: LED2.anode, Part1.ICSP_MOSI, Part1.D11_PWM/MOSI
  N3: R1.Pin_0, Part1.D7, LED3.blue_anode
  N4: R1.Pin_1, R2.Pin_1, R3.Pin_1, Part1.GND, R7.Pin_0, R8.Pin_1
  N5: R2.Pin_0, Part1.D4, LED3.red_anode
  N6: R3.Pin_0, Part1.D6_PWM, LED3.green_anode
  N7: Part1.A0, R6.pin_1, R8.Pin_0
  N8: Part1.5V, R4.Pin_0, R5.Pin_0, R6.pin_0, LED3.common_cathode
  N9: Part1.D8, R4.Pin_1, SW1.2
  N10: Part1.D9_PWM, R5.Pin_1, SW1.3
