# Fritzing sketch updating (saved by Fritzing 0.9.2b)

parts:
  Part1 = Arduino Uno (Rev3) - ICSP
  R1 = Resistor [tolerance=±5% resistance=330 package=THT]
  R2 = Resistor [tolerance=±5% resistance=330 package=THT]
  R3 = Resistor [tolerance=±5% resistance=330 package=THT]
  LED1 = RGB LED (com. cathode, rgb) [package="5 mm [THT]"]
  S2 = Toggle Switch [package=THT]
  S3 = Toggle Switch [package=THT]

nets:
  N1: Part1.5V, LED1.common_cathode
  N2: Part1.D8, S2.COM
  N3: Part1.D9_PWM, S3.COM
  N4: Part1.D7, R3.Pin_0
  N5: R1.Pin_1, LED1.red_anode
  N6: R2.Pin_1, LED1.blue_anode
  N7: R3.Pin_1, LED1.green_anode
