# Fritzing sketch Lab2-Fritzing-Schematic (saved by Fritzing 0.9.2b)
breadboards: 1

parts:
  Part1 = Arduino Uno (Rev3)
  LED1 = LED - 3mm [color="Red (633nm)" package="3 mm [THT]"]
  7_Segment2 = 7 Segment Display
  R2 = Resistor [tolerance=±5% resistance=330 package=THT]
  R4 = Resistor [tolerance=±5% resistance=3.0k package=THT]
  R5 = Resistor [tolerance=±5% resistance=3.0k package=THT]
  R6 = Resistor [tolerance=±5% resistance=3.0k package=THT]
  R21 = Resistor [tolerance=±5% resistance=3.0k package=THT]
  R22 = Resistor [tolerance=±5% resistance=330 package=THT]
  R23 = Resistor [tolerance=±5% resistance=3.0k package=THT]
  R24 = Resistor [tolerance=±5% resistance=3.0k package=THT]
  J1 = Piezo Speaker
  R25 = Resistor [tolerance=±5% resistance=10k package=THT]
  R1 = Resistor [tolerance=±5% resistance=330 package=THT]

nets:
  N1: Part1.D8, R21.Pin_1
  N2: Part1.D9_PWM, R22.Pin_1
  N3: Part1.D10_PWM/SS, R23.Pin_1
  N4: Part1.D11_PWM/MOSI, R25.Pin_1
  N5: Part1.D12/MISO, R24.Pin_1
  N6: Part1.GND, J1.pin1, R1.Pin_1
  N7: Part1.D2, LED1.cathode
  N8: Part1.D3_PWM, R2.Pin_1
  N9: Part1.D4, R6.Pin_1
  N10: Part1.D5_PWM, R4.Pin_1
  N11: Part1.D6_PWM, R5.Pin_1
  N12: Part1.5V, 7_Segment2.Segment_D, 7_Segment2.Segment_DP
  N13: LED1.anode, R1.Pin_0
  N14: 7_Segment2.Segment_G, R21.Pin_0
  N15: 7_Segment2.Segment_F, R22.Pin_0
  N16: 7_Segment2.common_anode, R4.Pin_0, R23.Pin_0
  N17: 7_Segment2.Segment_E, R24.Pin_0
  N18: 7_Segment2.Segment_C, R5.Pin_0
  N19: 7_Segment2.Segment_B, R6.Pin_0
  N20: 7_Segment2.Segment_A, R2.Pin_0
  N21: J1.pin2, R25.Pin_0
