# Fritzing sketch lab3 (saved by Fritzing 0.9.2b)
breadboards: 1

parts:
  Part1 = Arduino Uno (Rev3) - ICSP
  U1 = LCD-16X2 [package=lcd-16x2_noholes]
  R1 = Resistor [tolerance=±5% resistance=220 package=THT]
  U2 = POT [package=3362u]
  kEYPAD_MATRICIAL_1 = KEYPAD 4x3

nets:
  N1: Part1.A0, kEYPAD_MATRICIAL_1.col2
  N2: Part1.A1, kEYPAD_MATRICIAL_1.col3
  N3: Part1.A2, kEYPAD_MATRICIAL_1.arrow1
  N4: Part1.A3, kEYPAD_MATRICIAL_1.arrow2
  N5: Part1.A4/SDA, kEYPAD_MATRICIAL_1.arrow3
  N6: Part1.A5/SCL, kEYPAD_MATRICIAL_1.arrow4
  GND: Part1.GND, U1.VSS, U1.R_W, U1.K, U2.A
  N7: Part1.D8, kEYPAD_MATRICIAL_1.col1
  N8: Part1.D11_PWM/MOSI, U1.E
  N9: Part1.D12/MISO, U1.RS
  N10: Part1.D2, U1.DB7
  N11: Part1.D3_PWM, U1.DB6
  N12: Part1.D4, U1.DB5
  N13: Part1.D5_PWM, U1.DB4
  5V: Part1.5V, U1.VDD, R1.Pin_1, U2.E
  N14: U1.VO, U2.S
  N15: U1.A, R1.Pin_0

custom parts:
  KEYPAD 4x3: KEYPAD matricial de 12 botones, 4 filas x 3 columnas
