# Fritzing sketch lab4 (saved by Fritzing 0.9.2b)
breadboards: 1

parts:
  Part1 = Arduino Uno (Rev3) - ICSP
  S1 = Round Pushbutton
  RHT1 = Humidity and Temperature Sensor RHT03
  R2 = PHOTOCELL [package=photocell]
  R3 = Resistor [tolerance=±5% resistance=10k package=THT]
  R4 = Resistor [tolerance=±5% resistance=220 package=THT]
  T1 = LM35 Temperature Sensor [package="TO92 [THT]"]
  R5 = Resistor [tolerance=±5% resistance=220 package=THT]

nets:
  N1: Part1.A0, T1.Vout
  N2: Part1.A5/SCL, R2.P$2, R5.Pin_0
  N3: Part1.D2, RHT1.Data-signal, R3.Pin_0
  N4: Part1.D4, S1.leg1, R4.Pin_0
  5V: Part1.5V, S1.leg0, RHT1.Vcc, R2.P$1, R3.Pin_1, T1.+Vs
  GND: Part1.GND, RHT1.GND_2, R4.Pin_1, T1.GND, R5.Pin_1
