# Fritzing sketch Lab5 (saved by Fritzing 0.9.2b)
breadboards: 1

parts:
  Part1 = Arduino Uno (Rev3)
  T1 = TMP36 Temperature Sensor [package="TO92 [THT]"]
  R1 = Resistor [tolerance=±5% resistance=2k package=THT]
  Part2 = SRF05 Ultrasonic Rangefinder

nets:
  N1: Part1.A2, R1.Pin_1
  N2: Part1.D8, Part2.Trig
  N3: Part1.D6_PWM, Part2.Echo
  N4: Part1.5V, T1.Vout, R1.Pin_0
  GND: Part1.GND, T1.GND
