# Fritzing sketch Lab6 (saved by Fritzing 0.9.2b)
breadboards: 1

parts:
  Part1 = Arduino Uno (Rev3)
  S1 = Square Pushbutton
  R1 = Resistor [tolerance=±5% resistance=220 package=THT]

nets:
  N1: Part1.D2, R1.Pin_0
  N2: Part1.GND, S1.leg1, R1.Pin_1

notes:
  To the power of signal Generator
  To ground of Signal Generator
