# Fritzing sketch project2 (saved by Fritzing 0.9.2b)
breadboards: 1

parts:
  LED1 = RGB LED - (4 legs) [package="5 mm [THT]"]
  LED2 = LED - 3mm [color="Red (633nm)" package="3 mm [THT]"]
  T1 = LM35 Temperature Sensor [package="TO92 [THT]"]
  J1 = Piezo Speaker
  J2 = Basic Servo
  Part1 = Arduino Uno (Rev3) - ICSP
  R1 = Resistor [tolerance=±5% resistance=220 package="0402 [SMD]"]
  R2 = Resistor [tolerance=±5% resistance=220 package="2512 [SMD]"]
  R3 = Resistor [tolerance=±5% resistance=220 package="2512 [SMD]"]
  R4 = Resistor [tolerance=±5% resistance=220 package="2512 [SMD]"]
  R5 = Resistor [tolerance=±5% resistance=220 package="0402 [SMD]"]
  Part2 = SRF05 Ultrasonic Rangefinder
  Part3 = SRF05 Ultrasonic Rangefinder
  kEYPAD_MATRICIAL_1 = KEYPAD 4x3
  Raspberry_Pi_1 = Raspberry Pi 3  # not connected
  USBTTL2 = USB TTL Serial Cable  # not connected

nets:
  N1: LED1.red_cathode, R4.Pin_0
  N2: LED1.green_cathode, R3.Pin_0
  N3: LED1.blue_cathode, R2.Pin_1
  GND: LED2.cathode, T1.GND, R1.Pin_0, Part2.GND, Part3.GND
  N4: LED2.anode, R5.Pin_0
  VCC: T1.+Vs, J1.pin2, Part2.VCC, Part3.VCC
  N5: T1.Vout, Part1.A0
  N6: J1.pin1, Part1.D9_PWM, R1.Pin_1
  N7: J2.pulse, Part1.A1
  N8: Part1.A2, Part3.Trig
  N9: Part1.A3, Part3.Echo
  N10: Part1.ICSP_MISO, Part1.D12/MISO, R3.Pin_1
  N11: Part1.ICSP_MOSI, Part1.D11_PWM/MOSI, R4.Pin_1
  N12: Part1.D8, kEYPAD_MATRICIAL_1.col3
  N13: Part1.D10_PWM/SS, R5.Pin_1
  N14: Part1.D13/SCK, R2.Pin_0
  N15: Part1.D2, kEYPAD_MATRICIAL_1.arrow1
  N16: Part1.D3_PWM, kEYPAD_MATRICIAL_1.arrow2
  N17: Part1.D4, kEYPAD_MATRICIAL_1.arrow3
  N18: Part1.D5_PWM, kEYPAD_MATRICIAL_1.arrow4
  N19: Part1.D6_PWM, kEYPAD_MATRICIAL_1.col1
  N20: Part1.D7, kEYPAD_MATRICIAL_1.col2

notes:
  Mini Webcam

custom parts:
  KEYPAD 4x3: KEYPAD matricial de 12 botones, 4 filas x 3 columnas
